// Logisim project nand get.circ as structural Verilog: 1 circuit, main circuit main
module main (
  input  in_1,
  input  in_2
);

  wire and_1_out, nand_1_out, not_1_out;

  and and_1 (and_1_out, in_1, in_2);
  nand nand_1 (nand_1_out, in_1, in_2);
  not not_1 (not_1_out, and_1_out);
  LED led_1 (.in(nand_1_out));
  LED led_2 (.in(not_1_out));
endmodule
