// Logisim project news.circ as structural Verilog: 1 circuit, main circuit main
module main (
  input  in_1,
  input  in_2
);

  wire nor_1_out, not_1_out, or_1_out;

  nor nor_1 (nor_1_out, in_1, in_2);
  or or_1 (or_1_out, in_1, in_2);
  LED led_1 (.in(nor_1_out));
  not not_1 (not_1_out, or_1_out);
  LED led_2 (.in(not_1_out));
endmodule
